# Fritzing sketch jhagmag (saved by Fritzing 0.9.5d)
breadboards: 1

parts:
  Part1 = Arduino Uno (Rev3) - ICSP
  Q1 = MOSFET-NCHANNEL [package=to220v]
  Q2 = MOSFET-NCHANNEL [package=to220v]
  Q3 = MOSFET-NCHANNEL [package=to220v]
  S1 = Pushbutton [package="[THT]"]
  R1 = Resistor [tolerance=±5% resistance=220 package="0402 [SMD]"]
  R2 = Resistor [tolerance=±5% resistance=220 package="0402 [SMD]"]
  R3 = Resistor [tolerance=±5% resistance=220 package="0402 [SMD]"]
  R4 = Resistor [tolerance=±20% resistance=10000 package="0402 [SMD]"]
  R5 = Resistor [tolerance=±20% resistance=10000 package="0402 [SMD]"]
  R6 = Resistor [tolerance=±20% resistance=10000 package="0402 [SMD]"]
  Part2 = Bluetooth HC-05 Macho
  Power_plug1 = Power plug
  LED1 = RGB LED (com. cathode, rgb) [package="5 mm [THT]"]  # not connected

nets:
  N1: Part1.D8, S1.Pin_3, S1.Pin_4
  N2: Part1.D9_PWM, R3.Pin_0
  N3: Part1.D10_PWM/SS, R2.Pin_0
  N4: Part1.D11_PWM/MOSI, R1.Pin_0
  N5: Part1.D4, Part2.TXD
  N6: Part1.D5_PWM, Part2.RXD
  5V: Part1.5V, S1.Pin_1, S1.Pin_2, Part2.VCC
  GND: Part1.GND, Part2.GND
  N7: Q1.G, R3.Pin_1, R6.Pin_0
  N8: Q1.S, Q2.S, Q3.S, R4.Pin_1, R5.Pin_1, R6.Pin_1, Power_plug1.GND
  N9: Q2.G, R2.Pin_1, R5.Pin_0
  N10: Q3.G, R1.Pin_1, R4.Pin_0
